# Fritzing sketch Fritzing Sketch (saved by Fritzing 0.9.3b)

parts:
  Part1 = Arduino Mega ADK (Rev3)
  RE1 = KY-040 Rotary encoder [package=THT]
  RE2 = KY-040 Rotary encoder [package=THT]
  Part2 = Thumb Joystick

nets:
  N1: Part1.A0, Part2.HORZ
  N2: Part1.A1, Part2.VERT
  N3: Part1.D19/RX1, RE1.CLK
  N4: Part1.D18/TX1, RE1.DT
  N5: Part1.D17/RX2, RE1.SW
  VCC: Part1.5V, RE1.Vcc, RE2.Vcc, Part2.VCC
  GND: Part1.GND, RE1.GND, RE2.GND, Part2.GND
  N6: Part1.D2_PWM, RE2.CLK
  N7: Part1.D3_PWM, RE2.DT
  N8: Part1.D4_PWM, RE2.SW

custom parts:
  KY-040 Rotary encoder: KY-040 Rotary Encoder with switch on breakout borad from AZ Delivery
